# Fritzing sketch nrf24_hand_control_5jcEeCP8a3 (saved by Fritzing 0.9.3b)

parts:
  Nano1 = Arduino Nano v2.3
  Part2 = NRF24L01+ Breakout Board
  PWM1 = PCA9685 16x12-bit PWM Breakout
  J1 = Basic Servo

nets:
  GND: Nano1.GND, Part2.GND, PWM1.no_name_yet#501, PWM1.no_name_yet#701, PWM1.no_name_yet#1000, J1.gnd
  N1: Nano1.D8, Part2.CS
  N2: Nano1.D9, Part2.CE
  N3: Nano1.D11, Part2.MOSI
  N4: Nano1.D12, Part2.MISO
  N5: Nano1.D13, Part2.SCK
  3V3: Nano1.3V3, Part2.VCC
  N6: Nano1.A5, PWM1.no_name_yet#503
  N7: Nano1.A4, PWM1.no_name_yet#504
  N8: Nano1.+5V, PWM1.no_name_yet#505
  N9: PWM1.no_name_yet#0, J1.pulse
  N10: PWM1.no_name_yet#100, PWM1.no_name_yet#706, J1.vcc

notes:
  To high amp 5V supply
  5 Servos to channels 0-4
